// Logisim project LC-2200-16.circ as structural Verilog: 5 circuits, main circuit main
// DrMEM
module main (
);

  wire clear, clock, comparator_1_eq, DrALU, DrMEM, DrOFF, DrPC, DrREG, LdA, LdB, LdIR, LdMAR, LdPC, LdZ,
       WrMEM, WrREG, Z;
  wire [1:0] func, regselec;
  wire [2:0] opcode;
  wire [3:0] regno;
  wire [12:0] IR_q;
  wire [15:0] A_q, alu_1_out, B_q, bit_extender_1_out, controlled_buffer_1_out, MAR_q, PC_q, ram_1_data,
       register_file_1_dout;

  Register #(.width(16)) PC (.D(controlled_buffer_1_out), .en(LdPC), .Q(PC_q), .clk(clock), .clr(clear));
  assign controlled_buffer_1_out = DrPC ? PC_q : 16'bz;  // Controlled_Buffer controlled_buffer_1
  Comparator #(.width(16)) comparator_1 (
    .a({16{1'b0}}), .b(controlled_buffer_1_out), .eq(comparator_1_eq));  // open: gt, lt
  Register #(.width(1)) u_Z (.D(comparator_1_eq), .en(LdZ), .Q(Z), .clk(clock), .clr(clear));
  Register #(.width(16)) A (.D(controlled_buffer_1_out), .en(LdA), .Q(A_q), .clk(clock), .clr(clear));
  Register #(.width(16)) B (.D(controlled_buffer_1_out), .en(LdB), .Q(B_q), .clk(clock), .clr(clear));
  ALU alu_1 (.A(A_q), .OUT(alu_1_out), .func(func), .B(B_q));
  assign controlled_buffer_1_out = DrALU ? alu_1_out : 16'bz;  // Controlled_Buffer controlled_buffer_2
  Clock clock_1 (.out(clock));
  Button button_1 (.out(clear));
  register_file register_file_1 (
    .regno(regno), .WrREG(WrREG), .Din(controlled_buffer_1_out), .clock(clock), .Dout(register_file_1_dout));
  assign controlled_buffer_1_out = DrREG ? register_file_1_dout : 16'bz;  // Controlled_Buffer controlled_buffer_3
  Microcontrol microcontrol_1 (
    .IR(opcode), .Z(Z), .clk(clock), .DrREG(DrREG), .DrMEM(DrMEM), .DrALU(DrALU), .DrPC(DrPC), .DrOFF(DrOFF),
    .LdPC(LdPC), .LdIR(LdIR), .LdMAR(LdMAR), .LdA(LdA), .LdB(LdB), .LdZ(LdZ), .WrREG(WrREG), .WrMEM(WrMEM),
    .regselec(regselec), .func(func));
  Register #(.width(16)) MAR (.D(controlled_buffer_1_out), .en(LdMAR), .Q(MAR_q), .clk(clock), .clr(clear));
  RAM #(.addrWidth(16), .dataWidth(16), .bus("separate")) ram_1 (
    .addr(MAR_q), .din(controlled_buffer_1_out), .data(ram_1_data), .str(WrMEM), .clk(clock), .clr(clear));  // open: sel, ld
  Register #(.width(16)) IR (.D(controlled_buffer_1_out), .en(LdIR), .Q({opcode, IR_q}), .clk(clock), .clr(clear));
  assign controlled_buffer_1_out = DrMEM ? ram_1_data : 16'bz;  // Controlled_Buffer controlled_buffer_4
  assign bit_extender_1_out = {{11{IR_q[4]}}, IR_q[4:0]};  // Bit_Extender bit_extender_1
  assign controlled_buffer_1_out = DrOFF ? bit_extender_1_out : 16'bz;  // Controlled_Buffer controlled_buffer_5
  // Probe on IR_q[4:1]
  Multiplexer #(.select(2), .width(4)) multiplexer_1 (
    .in0(IR_q[12:9]), .in1(IR_q[8:5]), .in2(IR_q[4:1]), .out(regno), .sel(regselec));  // open: in3, en
endmodule

module ALU (
  input  [15:0] B,
  input  [15:0] A,
  input  [1:0] func,
  output [15:0] OUT
);

  wire [15:0] adder_1_out, adder_2_out, nand_1_out, subtractor_1_out;

  Adder #(.width(16)) adder_1 (.a(A), .b(B), .out(adder_1_out));  // open: cin, cout
  assign nand_1_out = ~(A & B);  // NAND_Gate nand_1, 16 bits wide
  Subtractor #(.width(16)) subtractor_1 (.a(A), .b(B), .out(subtractor_1_out));  // open: bin, bout
  Adder #(.width(16)) adder_2 (.a(A), .b(16'h1), .out(adder_2_out));  // open: cin, cout
  Multiplexer #(.select(2), .width(16), .enable("false")) multiplexer_1 (
    .in0(adder_1_out), .in1(nand_1_out), .in2(subtractor_1_out), .in3(adder_2_out), .out(OUT), .sel(func));
endmodule

module register_file (
  input  [3:0] regno,
  input  WrREG,
  input  [15:0] Din,
  input  clock,
  output [15:0] Dout
);

  wire demultiplexer_1_out1, demultiplexer_1_out2, demultiplexer_1_out3, demultiplexer_1_out4,
       demultiplexer_1_out5, demultiplexer_1_out6, demultiplexer_1_out7, demultiplexer_1_out8,
       demultiplexer_1_out9, demultiplexer_1_out10, demultiplexer_1_out11, demultiplexer_1_out12,
       demultiplexer_1_out13, demultiplexer_1_out14, demultiplexer_1_out15;
  wire [15:0] register_1_q, register_2_q, register_3_q, register_4_q, register_5_q, register_6_q,
       register_7_q, register_8_q, register_9_q, register_10_q, register_11_q, register_12_q, register_13_q,
       register_14_q, register_15_q, register_16_q;

  Demultiplexer #(.select(4), .enable("false")) demultiplexer_1 (
    .out1(demultiplexer_1_out1), .out2(demultiplexer_1_out2), .out3(demultiplexer_1_out3),
    .out4(demultiplexer_1_out4), .out5(demultiplexer_1_out5), .out6(demultiplexer_1_out6),
    .out7(demultiplexer_1_out7), .out8(demultiplexer_1_out8), .out9(demultiplexer_1_out9),
    .out10(demultiplexer_1_out10), .out11(demultiplexer_1_out11), .out12(demultiplexer_1_out12),
    .out13(demultiplexer_1_out13), .out14(demultiplexer_1_out14), .out15(demultiplexer_1_out15), .in(WrREG),
    .sel(regno));  // open: out0
  Register #(.width(16)) register_1 (.D(Din), .en(1'b0), .Q(register_1_q), .clk(clock));  // open: clr
  Register #(.width(16)) register_2 (.D(Din), .en(demultiplexer_1_out1), .Q(register_2_q), .clk(clock));  // open: clr
  Register #(.width(16)) register_3 (.D(Din), .en(demultiplexer_1_out2), .Q(register_3_q), .clk(clock));  // open: clr
  Register #(.width(16)) register_4 (.D(Din), .en(demultiplexer_1_out3), .Q(register_4_q), .clk(clock));  // open: clr
  Register #(.width(16)) register_5 (.D(Din), .en(demultiplexer_1_out4), .Q(register_5_q), .clk(clock));  // open: clr
  Register #(.width(16)) register_6 (.D(Din), .en(demultiplexer_1_out5), .Q(register_6_q), .clk(clock));  // open: clr
  Register #(.width(16)) register_7 (.D(Din), .en(demultiplexer_1_out6), .Q(register_7_q), .clk(clock));  // open: clr
  Register #(.width(16)) register_8 (.D(Din), .en(demultiplexer_1_out7), .Q(register_8_q), .clk(clock));  // open: clr
  Register #(.width(16)) register_9 (.D(Din), .en(demultiplexer_1_out8), .Q(register_9_q), .clk(clock));  // open: clr
  Register #(.width(16)) register_10 (.D(Din), .en(demultiplexer_1_out9), .Q(register_10_q), .clk(clock));  // open: clr
  Register #(.width(16)) register_11 (
    .D(Din), .en(demultiplexer_1_out10), .Q(register_11_q), .clk(clock));  // open: clr
  Register #(.width(16)) register_12 (
    .D(Din), .en(demultiplexer_1_out11), .Q(register_12_q), .clk(clock));  // open: clr
  Register #(.width(16)) register_13 (
    .D(Din), .en(demultiplexer_1_out12), .Q(register_13_q), .clk(clock));  // open: clr
  Register #(.width(16)) register_14 (
    .D(Din), .en(demultiplexer_1_out13), .Q(register_14_q), .clk(clock));  // open: clr
  Register #(.width(16)) register_15 (
    .D(Din), .en(demultiplexer_1_out14), .Q(register_15_q), .clk(clock));  // open: clr
  Register #(.width(16)) register_16 (
    .D(Din), .en(demultiplexer_1_out15), .Q(register_16_q), .clk(clock));  // open: clr
  Multiplexer #(.select(4), .width(16)) multiplexer_1 (
    .in0(register_1_q), .in1(register_2_q), .in2(register_3_q), .in3(register_4_q), .in4(register_5_q),
    .in5(register_6_q), .in6(register_7_q), .in7(register_8_q), .in8(register_9_q), .in9(register_10_q),
    .in10(register_11_q), .in11(register_12_q), .in12(register_13_q), .in13(register_14_q),
    .in14(register_15_q), .in15(register_16_q), .out(Dout), .sel(regno));  // open: en
  // Probe on Dout
endmodule

module _0 (
  input  [15:0] \input ,
  output out
);

  Comparator #(.width(16)) comparator_1 (.a({16{1'b0}}), .b(\input ), .eq(out));  // open: gt, lt
endmodule

module Microcontrol (
  input  [2:0] IR,
  input  Z,
  input  clk,
  output DrREG,
  output DrMEM,
  output DrALU,
  output DrPC,
  output DrOFF,
  output LdPC,
  output LdIR,
  output LdMAR,
  output LdA,
  output LdB,
  output LdZ,
  output WrREG,
  output WrMEM,
  output [1:0] regselec,
  output [1:0] func
);

  wire [1:0] muxSele;
  wire [5:0] multiplexer_1_out, register_1_q, rom_1_data, rom_2_data, rom_3_data;

  ROM #(.addrWidth(3), .dataWidth(6)) rom_1 (.addr(IR), .data(rom_1_data));  // open: sel
  ROM #(.addrWidth(2), .dataWidth(6)) rom_2 (.addr({1'b0, Z}), .data(rom_2_data));  // open: sel
  Multiplexer #(.select(2), .width(6)) multiplexer_1 (
    .in0(rom_3_data), .in1(rom_1_data), .in2(rom_2_data), .out(multiplexer_1_out), .sel(muxSele));  // open: in3, en
  Register #(.width(6)) register_1 (.D(multiplexer_1_out), .Q(register_1_q), .clk(clk));  // open: en, clr
  ROM #(.addrWidth(6), .dataWidth(25)) rom_3 (
    .addr(register_1_q),
    .data({muxSele, func, regselec, WrMEM, WrREG, LdZ, LdB, LdA, LdMAR, LdIR, LdPC, DrOFF, DrPC, DrALU, DrMEM, DrREG, rom_3_data}));  // open: sel

  // Other names for the same wires on the sheet: clock = clk

  // Notes on the sheet:
  //   contents of rom_1 (hex, n*v repeats v):
  //   3 6 9 c 10 14 1a 1c
  //   contents of rom_2 (hex, n*v repeats v):
  //   0 18
  //   contents of rom_3 (hex, n*v repeats v):
  //   6201 1082 e00900 84044 108045 20100 84047 108048 220100 8404a 840b 20100 8404d 840e 210f 20080 84051
  //   8412 2113 40040 4055 88056 410117 1004218 8419 900 a021b 840 1c 1d
endmodule
