// Logisim project Li_Lingyi_part2.circ as structural Verilog
module main (
);

  wire beq, beq_flush, can_Stall, CK, Clr, ClrStall, comparator_1_eq, comparator_2_eq, DBUF_rz_imme, flush1,
       isD, isM, isSW, jalr, mem_wb_buffer_1_alu_mem, not_1_out, re_sel, SelPC, SelX_FBUF, SelY_FBUF, selZ,
       Stall, Wr_Ld, WrEN;
  wire [1:0] forward_y, forward_z, func;
  wire [3:0] mem_wb_buffer_1_rx, multiplexer_3_out, multiplexer_4_out, opcode_DBUF, opcode_EBUF, opcode_FBUF,
       register_index, Rx_specifier_DBUF, Rx_specifier_EBUF, Rx_specifier_FBUF, ry_MBUF, Ry_specifier_DBUF,
       Ry_specifier_EBUF, Ry_specifier_FBUF, Rz_specifier_DBUF, Rz_specifier_FBUF;
  wire [19:0] imme;
  wire [31:0] adder_2_out, adder_3_out, ALU_out, data_in, data_out, imme_EBUF, imme_extend, imme_extend_DBUF,
       incremeted_PC, Instruction, mem_wb_buffer_1_aluresult_2, mem_wb_buffer_1_data_2, MFB,
       multiplexer_1_out, multiplexer_5_out, multiplexer_8_out, PC_1, PC_DBUF, PC_EBUF, PC_FBUF, PC_from_PC,
       ram_1_data, result_, Ry_value, Ry_value_DBUF, Ry_value_out, Rz_value, Rz_value_DBUF, seld_Ry_value,
       seld_Ry_value_again, seld_Ry_value_again_again, seld_Rz_value, Sw_Sel;

  Register #(.width(32)) PC (.D(multiplexer_5_out), .en(CK), .Q(PC_from_PC), .clk(CK));  // open: clr
  Button button_1 (.out(Clr));
  Adder #(.width(32)) adder_1 (.a(32'h1), .b(PC_from_PC), .out(incremeted_PC));  // open: cin, cout
  Clock CLOCK (.out(CK));
  not not_1 (not_1_out, Stall);
  Adder #(.width(32)) adder_2 (.a(PC_EBUF), .b(32'h1), .out(adder_2_out));  // open: cin, cout
  RAM #(.addrWidth(24), .dataWidth(32)) ram_1 (
    .addr(PC_from_PC[23:0]), .data(ram_1_data), .sel(not_1_out), .clk(CK));  // open: ld, clr
  IF_IDRR_Buffer FBUF (
    .in_1(CK), .PC(PC_from_PC), .Addr_in(Instruction), .PC_out(PC_FBUF), .Rz(Rz_specifier_FBUF),
    .Offset(imme), .Ry(Ry_specifier_FBUF), .Rx(Rx_specifier_FBUF), .opcode(opcode_FBUF), .in_4(flush1),
    .SelX(SelX_FBUF), .SelY(SelY_FBUF), .Stall(can_Stall), .isM(isM));
  Multiplexer #(.width(32), .enable("false")) multiplexer_1 (
    .in0(incremeted_PC), .in1(PC_from_PC), .out(multiplexer_1_out), .sel(Stall));
  Multiplexer #(.width(32), .enable("false")) multiplexer_2 (
    .in0(ram_1_data), .in1({32{1'b0}}), .out(Instruction), .sel(Stall));
  Multiplexer #(.width(4), .enable("false")) multiplexer_3 (
    .in0(Ry_specifier_FBUF), .in1(Rx_specifier_FBUF), .out(multiplexer_3_out), .sel(SelX_FBUF));
  Multiplexer #(.width(4), .enable("false")) multiplexer_4 (
    .in0(Rz_specifier_FBUF), .in1(Ry_specifier_FBUF), .out(multiplexer_4_out), .sel(SelY_FBUF));
  Adder #(.width(32)) adder_3 (.a(adder_2_out), .b(imme_EBUF), .out(adder_3_out));  // open: cin, cout
  // Probe on data_in
  Multiplexer #(.select(2), .width(32), .enable("false")) multiplexer_5 (
    .in0(multiplexer_1_out), .in1(Ry_value_out), .in2(adder_3_out), .in3(adder_3_out),
    .out(multiplexer_5_out), .sel({beq_flush, jalr}));
  Multiplexer #(.width(4), .enable("false")) multiplexer_6 (
    .in0(mem_wb_buffer_1_rx), .in1(ry_MBUF), .out(register_index), .sel(re_sel));
  // Probe on ry_MBUF
  // Probe on multiplexer_5_out
  // Probe on {beq_flush, jalr}
  assign imme_extend = {{12{imme[19]}}, imme};  // Bit_Extender bit_extender_1
  // Probe on multiplexer_3_out
  // Probe on multiplexer_4_out
  // Probe on seld_Ry_value
  Dual_Ported_Register_File dual_ported_register_file_1 (
    .CLK(CK), .WrREGNO(register_index), .RdREGNO1(multiplexer_3_out), .RdREGNO2(multiplexer_4_out),
    .INPUT(data_in), .OUT1(Ry_value), .OUT2(Rz_value), .WrEN(WrEN));
  // Probe on imme_extend
  // Probe on isD
  forward_unit forward_unit_1 (
    .Ry_spcifier_FBUF(multiplexer_3_out), .Rx_specifier_EBUF(Rx_specifier_EBUF),
    .Rz_spcifier_FBUF(multiplexer_4_out), .forward_y(forward_y), .forward_z(forward_z), .canStall(can_Stall),
    .Stall(Stall), .isM(isM), .Rx_DBUF(Rx_specifier_DBUF), .isD(isD), .jalr(SelPC),
    .Rx_specifier_FBUF(Rx_specifier_FBUF), .isSw(isSW));
  // Probe on seld_Rz_value
  Multiplexer #(.width(32), .enable("false")) multiplexer_7 (
    .in0(Ry_value_DBUF), .in1(Rz_value_DBUF), .out(seld_Ry_value_again), .sel(selZ));
  IDRR_EX_Buffer DBUF (
    .CK(CK), .Rx_Specifier(Rx_specifier_FBUF), .Ry(seld_Ry_value), .Rz(seld_Rz_value), .offSet(imme_extend),
    .opcode(opcode_FBUF), .PC(PC_FBUF), .Rx_out(Rx_specifier_DBUF), .Ry_out(Ry_value_DBUF),
    .Rz_out(Rz_value_DBUF), .offset_out(imme_extend_DBUF), .opcode_out(opcode_DBUF), .PC_out(PC_DBUF),
    .in_8(flush1), .Ry_specifier(Ry_specifier_FBUF), .Rz_specifier(Rz_specifier_FBUF),
    .out_17(Ry_specifier_DBUF), .out_18(Rz_specifier_DBUF), .Rz_Imme(DBUF_rz_imme), .jalr(SelPC),
    .FUNC(func), .sel_ry_rz(selZ), .isD(isD), .isSW(isSW));
  Multiplexer #(.width(32), .enable("false")) multiplexer_8 (
    .in0(Rz_value_DBUF), .in1(imme_extend_DBUF), .out(multiplexer_8_out), .sel(DBUF_rz_imme));
  // Probe on seld_Ry_value
  Multiplexer #(.select(2), .width(32), .enable("false")) multiplexer_9 (
    .in0(Ry_value), .in1(MFB), .in2(Sw_Sel), .in3(Sw_Sel), .out(seld_Ry_value), .sel(forward_y));
  // Probe on forward_y
  Multiplexer #(.select(2), .width(32), .enable("false")) multiplexer_10 (
    .in0(Rz_value), .in1(MFB), .in2(ALU_out), .in3(ALU_out), .out(seld_Rz_value), .sel(forward_z));
  // Probe on forward_z
  // Probe on seld_Ry_value_again_again
  // Probe on multiplexer_8_out
  // Probe on seld_Rz_value
  ALU alu_1 (.FUNC(func), .A(seld_Ry_value_again_again), .B(multiplexer_8_out), .OUT(ALU_out));
  // Probe on func
  Multiplexer #(.width(32), .enable("false")) multiplexer_11 (
    .in0(seld_Ry_value_again), .in1(PC_DBUF), .out(seld_Ry_value_again_again), .sel(SelPC));
  // Probe on ALU_out
  // Probe on imme_extend_DBUF
  EX_MEM_Buffer EBUF (
    .in_1(CK), .Rx_specifier(Rx_specifier_DBUF), .RESULTin(ALU_out), .Rz(Ry_value_DBUF),
    .opcode_in(opcode_DBUF), .EX_en(CK), .Rx_specifier_2(Rx_specifier_EBUF), .resultOut(PC_1),
    .RzOut(Ry_value_out), .opcode_out(opcode_EBUF), .in_7(Clr), .in_8(PC_DBUF), .out_15(PC_EBUF), .isM(isM),
    .ClrStall(ClrStall), .beq(beq), .imme(imme_extend_DBUF), .imme_out(imme_EBUF), .jalr(jalr),
    .Ry_specifier(Ry_specifier_DBUF), .Ry_specifier_out(Ry_specifier_EBUF), .Wr(Wr_Ld));  // open: istalll
  Comparator #(.width(32)) comparator_1 (.a(PC_1), .b({32{1'b0}}), .eq(comparator_1_eq));  // open: gt, lt
  Comparator #(.width(1)) comparator_2 (.a(beq), .b(1'b1), .eq(comparator_2_eq));  // open: gt, lt
  Multiplexer #(.width(32), .enable("false")) multiplexer_12 (
    .in0(ALU_out), .in1(Ry_value_DBUF), .out(Sw_Sel), .sel(isSW));
  // Probe on PC_1
  // Probe on imme_EBUF
  // Probe on comparator_1_eq
  ROM #(.addrWidth(4), .dataWidth(1)) rom_1 (.addr(opcode_EBUF));  // open: data, sel
  and and_1 (beq_flush, comparator_1_eq, comparator_2_eq);
  Multiplexer #(.width(32), .enable("false")) multiplexer_13 (.in0(PC_1), .in1(PC_1), .out(result_), .sel(jalr));
  // Probe on data_out
  DMEM dmem_1 (.ADDRESS(PC_1), .in_4(Wr_Ld), .DATA_OUT(data_out), .DATA_IN(Ry_value_out), .CLOCK(CK));
  or or_1 (flush1, beq_flush, jalr);
  Multiplexer #(.width(32), .enable("false")) multiplexer_14 (.in0(PC_1), .in1(data_out), .out(MFB), .sel(isM));
  MEM_WB_Buffer mem_wb_buffer_1 (
    .in_1(CK), .in_2(CK), .data(data_out), .Rx_specifier(Rx_specifier_EBUF), .ALUresult(result_),
    .opcode_in(opcode_EBUF), .Data_2(mem_wb_buffer_1_data_2), .Rx(mem_wb_buffer_1_rx),
    .ALUresult_2(mem_wb_buffer_1_aluresult_2), .ALU_MEM(mem_wb_buffer_1_alu_mem), .WrEn(WrEN), .jalr(re_sel),
    .ry(Ry_specifier_EBUF), .ry_2(ry_MBUF));  // open: ClrStall
  Multiplexer #(.width(32), .enable("false")) multiplexer_15 (
    .in0(mem_wb_buffer_1_aluresult_2), .in1(mem_wb_buffer_1_data_2), .out(data_in),
    .sel(mem_wb_buffer_1_alu_mem));
  // Probe on mem_wb_buffer_1_rx
  // Probe on data_in
  // Probe on Ry_specifier_EBUF

  // Other names for the same wires on the sheet: TB = beq_flush; EBUF_EN = CK; MBUF_EN = CK; result_EBUF[31:0] = PC_1;
  //   ZeroDetect[31:0] = PC_1; Rz_EBUF[31:0] = Ry_value_out

  // Notes on the sheet:
  //   contents of rom_1 (hex, n*v repeats v):
  //   5*0 1
endmodule

module Dual_Ported_Register_File (
  input  CLK,
  input  WrEN,
  input  [3:0] WrREGNO,
  input  [3:0] RdREGNO1,
  input  [3:0] RdREGNO2,
  input  [31:0] INPUT,
  output [31:0] OUT1,
  output [31:0] OUT2
);

  wire En_a0, En_a1, En_a2, En_a3, En_a4, En_at, En_fp, En_k0, En_ra, En_s0, En_s1, En_s2, En_s3, En_sp,
       En_v0;
  wire [31:0] a0, a1, a2, a3, a4, at, fp, k0, ra, s0, s1, s2, s3, sp, v0, zero;

  Decoder #(.select(4), .disabled(0)) decoder_1 (
    .out1(En_at), .out2(En_v0), .out3(En_a0), .out4(En_a1), .out5(En_a2), .out6(En_a3), .out7(En_a4),
    .out8(En_s0), .out9(En_s1), .out10(En_s2), .out11(En_s3), .out12(En_k0), .out13(En_sp), .out14(En_fp),
    .out15(En_ra), .sel(WrREGNO), .en(WrEN));  // open: out0
  Register #(.width(32)) u_zero (.D(INPUT), .en(1'b0), .Q(zero), .clk(CLK));  // open: clr
  Register #(.width(32)) u_at (.D(INPUT), .en(En_at), .Q(at), .clk(CLK));  // open: clr
  Register #(.width(32)) u_v0 (.D(INPUT), .en(En_v0), .Q(v0), .clk(CLK));  // open: clr
  Register #(.width(32)) u_a0 (.D(INPUT), .en(En_a0), .Q(a0), .clk(CLK));  // open: clr
  // Probe on INPUT
  Register #(.width(32)) u_a1 (.D(INPUT), .en(En_a1), .Q(a1), .clk(CLK));  // open: clr
  Register #(.width(32)) u_a2 (.D(INPUT), .en(En_a2), .Q(a2), .clk(CLK));  // open: clr
  Register #(.width(32)) u_a3 (.D(INPUT), .en(En_a3), .Q(a3), .clk(CLK));  // open: clr
  Register #(.width(32)) u_a4 (.D(INPUT), .en(En_a4), .Q(a4), .clk(CLK));  // open: clr
  Multiplexer #(.select(4), .width(32), .disabled(0), .enable("false")) multiplexer_1 (
    .in0(zero), .in1(at), .in2(v0), .in3(a0), .in4(a1), .in5(a2), .in6(a3), .in7(a4), .in8(s0), .in9(s1),
    .in10(s2), .in11(s3), .in12(k0), .in13(sp), .in14(fp), .in15(ra), .out(OUT2), .sel(RdREGNO2));
  Register #(.width(32)) u_s0 (.D(INPUT), .en(En_s0), .Q(s0), .clk(CLK));  // open: clr
  Register #(.width(32)) u_s1 (.D(INPUT), .en(En_s1), .Q(s1), .clk(CLK));  // open: clr
  Register #(.width(32)) u_s2 (.D(INPUT), .en(En_s2), .Q(s2), .clk(CLK));  // open: clr
  Register #(.width(32)) u_s3 (.D(INPUT), .en(En_s3), .Q(s3), .clk(CLK));  // open: clr
  Register #(.width(32)) u_k0 (.D(INPUT), .en(En_k0), .Q(k0), .clk(CLK));  // open: clr
  Register #(.width(32)) u_sp (.D(INPUT), .en(En_sp), .Q(sp), .clk(CLK));  // open: clr
  Register #(.width(32)) u_fp (.D(INPUT), .en(En_fp), .Q(fp), .clk(CLK));  // open: clr
  Register #(.width(32)) u_ra (.D(INPUT), .en(En_ra), .Q(ra), .clk(CLK));  // open: clr
  Multiplexer #(.select(4), .width(32), .disabled(0), .enable("false")) multiplexer_2 (
    .in0(zero), .in1(at), .in2(v0), .in3(a0), .in4(a1), .in5(a2), .in6(a3), .in7(a4), .in8(s0), .in9(s1),
    .in10(s2), .in11(s3), .in12(k0), .in13(sp), .in14(fp), .in15(ra), .out(OUT1), .sel(RdREGNO1));

  // Notes on the sheet:
  //   DO NOT MODIFY THIS FILE
endmodule

module IF_IDRR_Buffer (
  input  in_1,
  input  [31:0] PC,
  input  [31:0] Addr_in,
  input  in_4,
  input  isM,
  output [31:0] PC_out,
  output [3:0] Rz,
  output [19:0] Offset,
  output [3:0] Ry,
  output [3:0] Rx,
  output [3:0] opcode,
  output SelX,
  output SelY,
  output Stall
);

  wire [2:2] rom_1_data;

  // Probe on Addr_in
  Register #(.width(32)) register_1 (.D(PC), .en(in_1), .Q(PC_out), .clk(in_1), .clr(in_4));
  Register #(.width(32)) register_2 (.D(Addr_in), .en(in_1), .Q({opcode, Rx, Ry, Offset}), .clk(in_1), .clr(in_4));
  ROM #(.addrWidth(4), .dataWidth(3)) rom_1 (.addr(opcode), .data({rom_1_data[2], SelY, SelX}));  // open: sel
  // Probe on PC_out
  Multiplexer #(.enable("false")) multiplexer_1 (.in0(rom_1_data[2]), .in1(1'b0), .out(Stall), .sel(isM));
  // Probe on Offset

  assign Rz = Offset[3:0];

  // Other names for the same wires on the sheet: flush = in_4; CK = in_1; IFEn = in_1

  // Notes on the sheet:
  //   contents of rom_1 (hex, n*v repeats v):
  //   0 0 0 4 3 3 3
endmodule

module IDRR_EX_Buffer (
  input  CK,
  input  [3:0] Rx_Specifier,
  input  [31:0] Ry,
  input  [31:0] Rz,
  input  [31:0] offSet,
  input  [3:0] opcode,
  input  [31:0] PC,
  input  in_8,
  input  [3:0] Ry_specifier,
  input  [3:0] Rz_specifier,
  output [3:0] Rx_out,
  output [31:0] Ry_out,
  output [31:0] Rz_out,
  output [31:0] offset_out,
  output [3:0] opcode_out,
  output [31:0] PC_out,
  output [3:0] out_17,
  output [3:0] out_18,
  output isD,
  output Rz_Imme,
  output jalr,
  output sel_ry_rz,
  output isSW,
  output [1:0] FUNC
);

  Register #(.width(4)) Rx (.D(Rx_Specifier), .en(CK), .Q(Rx_out), .clk(CK), .clr(in_8));
  Register #(.width(32)) u_Ry (.D(Ry), .en(CK), .Q(Ry_out), .clk(CK), .clr(in_8));
  Register #(.width(32)) u_Rz (.D(Rz), .en(CK), .Q(Rz_out), .clk(CK), .clr(in_8));
  Register #(.width(32)) u_offSet (.D(offSet), .en(CK), .Q(offset_out), .clk(CK), .clr(in_8));
  Register #(.width(4)) register_1 (.D(opcode), .en(CK), .Q(opcode_out), .clk(CK), .clr(in_8));
  Register #(.width(32)) u_PC (.D(PC), .en(CK), .Q(PC_out), .clk(CK), .clr(in_8));
  Register #(.width(4)) register_2 (.D(Ry_specifier), .en(CK), .Q(out_17), .clk(CK), .clr(in_8));
  Register #(.width(4)) register_3 (.D(Rz_specifier), .en(CK), .Q(out_18), .clk(CK), .clr(in_8));
  // Probe on isD
  ROM #(.addrWidth(4), .dataWidth(7)) rom_1 (
    .addr(opcode_out), .data({isSW, sel_ry_rz, FUNC, jalr, Rz_Imme, isD}));  // open: sel

  // Other names for the same wires on the sheet: En = CK; flush = in_8; OPcode_t[3:0] = opcode_out

  // Notes on the sheet:
  //   contents of rom_1 (hex, n*v repeats v):
  //   1 9 3 22 63 11 1d
endmodule

module EX_MEM_Buffer (
  input  in_1,
  input  [3:0] Rx_specifier,
  input  [31:0] RESULTin,
  input  [31:0] Rz,
  input  [3:0] opcode_in,
  input  EX_en,
  input  in_7,
  input  [31:0] in_8,
  input  [31:0] imme,
  input  [3:0] Ry_specifier,
  output [3:0] Rx_specifier_2,
  output [31:0] resultOut,
  output [31:0] RzOut,
  output [3:0] opcode_out,
  output [31:0] out_15,
  output Wr,
  output beq,
  output isM,
  output ClrStall,
  output jalr,
  output istalll,
  output [31:0] imme_out,
  output [3:0] Ry_specifier_out
);

  wire [2:2] rom_1_data;

  Register #(.width(4)) u_Rx_specifier (.D(Rx_specifier), .en(EX_en), .Q(Rx_specifier_2), .clk(in_1), .clr(in_7));
  Register #(.width(32)) result (.D(RESULTin), .en(EX_en), .Q(resultOut), .clk(in_1), .clr(in_7));
  Register #(.width(32)) u_Rz (.D(Rz), .en(EX_en), .Q(RzOut), .clk(in_1), .clr(in_7));
  Register #(.width(4)) opcode (.D(opcode_in), .en(EX_en), .Q(opcode_out), .clk(in_1), .clr(in_7));
  Register #(.width(32)) PC (.D(in_8), .en(EX_en), .Q(out_15), .clk(in_1), .clr(in_7));
  ROM #(.addrWidth(4), .dataWidth(6)) rom_1 (
    .addr(opcode_out), .data({istalll, jalr, ClrStall, rom_1_data[2], beq, Wr}));  // open: sel
  Register #(.width(32)) imme_extend (.D(imme), .en(EX_en), .Q(imme_out), .clk(in_1), .clr(in_7));
  Register #(.width(4)) register_1 (.D(Ry_specifier), .en(EX_en), .Q(Ry_specifier_out), .clk(in_1), .clr(in_7));
  // Probe on resultOut
  not not_1 (isM, rom_1_data[2]);

  // Other names for the same wires on the sheet: CK = in_1; Clear = in_7; EN = EX_en; OPcode[3:0] = opcode_out

  // Notes on the sheet:
  //   contents of rom_1 (hex, n*v repeats v):
  //   c c c 28 d e 3c
endmodule

// MBUF
module MEM_WB_Buffer (
  input  in_1,
  input  in_2,
  input  [31:0] data,
  input  [3:0] Rx_specifier,
  input  [31:0] ALUresult,
  input  [3:0] ry,
  input  [3:0] opcode_in,
  output [31:0] Data_2,
  output [3:0] Rx,
  output [31:0] ALUresult_2,
  output [3:0] ry_2,
  output ClrStall,
  output ALU_MEM,
  output WrEn,
  output jalr
);

  wire [3:0] register_1_q;

  Register #(.width(4)) register_1 (.D(opcode_in), .en(in_1), .Q(register_1_q), .clk(in_1));  // open: clr
  Register #(.width(32)) register_2 (.D(data), .en(in_2), .Q(Data_2), .clk(in_1));  // open: clr
  Register #(.width(4)) register_3 (.D(Rx_specifier), .en(in_2), .Q(Rx), .clk(in_1));  // open: clr
  Register #(.width(32)) register_4 (.D(ALUresult), .en(in_2), .Q(ALUresult_2), .clk(in_1));  // open: clr
  Register #(.width(4)) register_5 (.D(ry), .en(in_2), .Q(ry_2), .clk(in_1));  // open: clr
  ROM #(.addrWidth(4), .dataWidth(4)) rom_1 (.addr(register_1_q), .data({jalr, WrEn, ClrStall, ALU_MEM}));  // open: sel
  // Probe on nothing

  // Other names for the same wires on the sheet: CK = in_1; MEM_EN = in_2

  // Notes on the sheet:
  //   contents of rom_1 (hex, n*v repeats v):
  //   6 6 6 7 2 2 e
endmodule

module ALU (
  input  [1:0] FUNC,
  input  [31:0] A,
  input  [31:0] B,
  output [31:0] OUT
);

  wire [31:0] adder_1_out, adder_2_out, nand_1_out, subtractor_1_out;

  Adder #(.width(32)) adder_1 (.a(A), .b(B), .out(adder_1_out), .cin(1'b0));  // open: cout
  assign nand_1_out = ~(A & B);  // NAND_Gate nand_1, 32 bits wide
  Subtractor #(.width(32)) subtractor_1 (.a(A), .b(B), .out(subtractor_1_out), .bin(1'b0));  // open: bout
  Adder #(.width(32)) adder_2 (.a(A), .b({32{1'b0}}), .out(adder_2_out), .cin(1'b1));  // open: cout
  // Probe on OUT
  Multiplexer #(.select(2), .width(32), .disabled(0), .enable("false")) multiplexer_1 (
    .in0(adder_1_out), .in1(nand_1_out), .in2(subtractor_1_out), .in3(adder_2_out), .out(OUT), .sel(FUNC));

  // Notes on the sheet:
  //   DO NOT MODIFY THIS
endmodule

module IMEM (
  input  [31:0] PCin,
  output [31:0] out
);

  RAM #(.addrWidth(24), .dataWidth(32)) ram_1 (.addr(PCin[23:0]), .data(out), .ld(1'b1));  // open: sel, clk, clr
endmodule

// mem
module DMEM (
  input  [31:0] DATA_IN,
  input  [31:0] ADDRESS,
  input  CLOCK,
  input  in_4,
  output [31:0] DATA_OUT
);

  wire not_1_out;

  not not_1 (not_1_out, in_4);
  RAM #(.addrWidth(24), .dataWidth(32), .bus("separate")) ram_1 (
    .addr(ADDRESS[23:0]), .din(DATA_IN), .data(DATA_OUT), .str(in_4), .clk(CLOCK), .ld(not_1_out));  // open: sel, clr

  // Other names for the same wires on the sheet: PASS[31:0] = ADDRESS; TRASH[7:0] = ADDRESS[31:24]; Wr = in_4
endmodule

// Rx_DBUF
module forward_unit (
  input  [3:0] Ry_spcifier_FBUF,
  input  [3:0] Rz_spcifier_FBUF,
  input  [3:0] Rx_DBUF,
  input  [3:0] Rx_specifier_EBUF,
  input  isSw,
  input  jalr,
  input  [3:0] Rx_specifier_FBUF,
  input  isD,
  input  isM,
  input  canStall,
  output [1:0] forward_y,
  output [1:0] forward_z,
  output Stall
);

  wire and_1_out, and_2_out, and_3_out, and_5_out, and_6_out, comparator_1_eq, comparator_2_eq,
       comparator_3_eq, comparator_4_eq, comparator_5_eq, comparator_6_eq, comparator_7_eq, comparator_8_eq,
       Ry_ALU;

  Comparator #(.width(4)) comparator_1 (
    .a(Rz_spcifier_FBUF), .b(Rx_specifier_EBUF), .eq(comparator_1_eq));  // open: gt, lt
  Comparator #(.width(4)) comparator_2 (
    .a(Ry_spcifier_FBUF), .b(Rx_specifier_EBUF), .eq(comparator_2_eq));  // open: gt, lt
  Comparator #(.width(4)) comparator_3 (.a(Rx_specifier_FBUF), .b(Rx_DBUF), .eq(comparator_3_eq));  // open: gt, lt
  and and_1 (and_1_out, comparator_3_eq, isSw);
  and and_2 (and_2_out, comparator_1_eq, isM);
  and and_3 (and_3_out, comparator_2_eq, isM);
  or or_1 (forward_y[1], Ry_ALU, and_1_out);
  or or_2 (forward_y[0], and_3_out, comparator_2_eq);
  or or_3 (forward_z[0], comparator_1_eq, and_2_out);
  Comparator #(.width(4)) comparator_4 (.a(Rx_DBUF), .b(Rx_specifier_EBUF), .eq(comparator_4_eq));  // open: gt, lt
  Comparator #(.width(4)) comparator_5 (.a(Rx_DBUF), .b(Ry_spcifier_FBUF), .eq(comparator_5_eq));  // open: gt, lt
  Comparator #(.width(4)) comparator_6 (.a(Rz_spcifier_FBUF), .b(Rx_DBUF), .eq(comparator_6_eq));  // open: gt, lt
  and and_4 (Stall, comparator_4_eq, canStall);
  Comparator #(.width(4)) comparator_7 (.a(Rx_DBUF), .b(Rx_specifier_EBUF), .eq(comparator_7_eq));  // open: gt, lt
  and and_5 (and_5_out, comparator_5_eq, isD);
  and and_6 (and_6_out, isD, comparator_6_eq);
  Comparator #(.width(4)) comparator_8 (.a(Rx_DBUF), .b(Rx_specifier_EBUF), .eq(comparator_8_eq));  // open: gt, lt
  Multiplexer #(.enable("false")) multiplexer_1 (.in0(and_5_out), .in1(comparator_7_eq), .out(Ry_ALU), .sel(jalr));
  Multiplexer #(.enable("false")) multiplexer_2 (
    .in0(and_6_out), .in1(comparator_8_eq), .out(forward_z[1]), .sel(jalr));

  // Other names for the same wires on the sheet: Ry_MEM = forward_y[0]; Rz_MEM = forward_z[0]; Rz_ALU = forward_z[1];
  //   Rx_EBUF[3:0] = Rx_specifier_EBUF; Rx_FBUF[3:0] = Rx_specifier_FBUF; Ry[3:0] = Ry_spcifier_FBUF;
  //   Rz[3:0] = Rz_spcifier_FBUF
endmodule

module more_register (
  input  clk,
  input  flush,
  input  [3:0] opcode,
  input  [31:0] pc,
  input  [31:0] imme,
  input  [3:0] rx,
  input  [3:0] ry,
  input  [3:0] rz,
  output [3:0] out_9,
  output [31:0] out_10,
  output [31:0] out_11,
  output [3:0] out_12,
  output [3:0] out_13,
  output [3:0] out_14
);

  Register #(.width(4)) u_opcode (.D(opcode), .en(clk), .Q(out_9), .clk(clk), .clr(flush));
  Register #(.width(32)) u_PC (.D(pc), .en(clk), .Q(out_10), .clk(clk), .clr(flush));
  Register #(.width(32)) u_imme (.D(imme), .en(clk), .Q(out_11), .clk(clk), .clr(flush));
  Register #(.width(4)) Rx_specifier (.D(rx), .en(clk), .Q(out_12), .clk(clk), .clr(flush));
  Register #(.width(4)) Ry_specifier (.D(ry), .en(clk), .Q(out_13), .clk(clk), .clr(flush));
  Register #(.width(4)) Rz_specifier (.D(rz), .en(clk), .Q(out_14), .clk(clk), .clr(flush));
endmodule
